// Digital circuit 4bit_Processor.dig as structural Verilog
module _4bit_Processor (
  input  clk
);

  wire and_1_out, and_2_out, and_5_out, write;
  wire [1:0] or_1_out, register_1_q, rom_1_d;
  wire [3:0] alu_1_output, IM_d, IR_q, multiplexer_1_out, multiplexer_2_out, pc_1_pc, RF_rdata1, RF_rdata2;
  wire [8:0] CU_out;

  and and_1 (and_1_out, ~CU_out[3], ~register_1_q[1]);  // And
  and and_2 (and_2_out, ~register_1_q[0], ~register_1_q[1]);  // And
  and and_3 (or_1_out[1], ~register_1_q[1], register_1_q[0]);  // And
  or or_1 (or_1_out[0], and_1_out, and_2_out);
  PC pc_1 (.clk(clk), .inc(rom_1_d[0]), .PC(pc_1_pc));
  and and_4 (write, ~or_1_out[0], ~or_1_out[1]);  // And
  Register #(.Bits(2)) register_1 (.D(or_1_out), .C(clk), .en(1'b1), .Q(register_1_q));
  // Probe on pc_1_pc
  ROM #(.AddrBits(4), .Bits(4)) IM (.A(pc_1_pc), .sel(1'b1), .D(IM_d));
  ROM #(.Bits(2)) rom_1 (.A(register_1_q), .sel(1'b1), .D(rom_1_d));
  Register #(.Bits(4)) IR (.D(IM_d), .C(clk), .en(rom_1_d[1]), .Q(IR_q));
  // Probe on IR_q
  // Probe on IM_d
  LookUpTable #(.Bits(9)) CU (.in0(IR_q[0]), .in1(IR_q[1]), .in2(IR_q[2]), .in3(IR_q[3]), .out(CU_out));
  and and_5 (and_5_out, write, CU_out[4]);
  Multiplexer #(.Bits(4)) multiplexer_1 (
    .sel(CU_out[3]), .in_0(multiplexer_2_out), .in_1(IM_d), .out(multiplexer_1_out));
  register_file RF (
    .wdata(multiplexer_1_out), .rd(CU_out[5]), .wen(and_5_out), .rs1(CU_out[7]), .rs2(CU_out[6]), .clk(clk),
    .rdata1(RF_rdata1), .rdata2(RF_rdata2));
  // Probe on RF_rdata1
  // Probe on RF_rdata2
  // Probe on multiplexer_2_out
  ALU alu_1 (.A(RF_rdata1), .B(RF_rdata2), .Control(CU_out[2:0]), .Output(alu_1_output));  // open: Z_Flag
  Multiplexer #(.Bits(4)) multiplexer_2 (
    .sel(CU_out[8]), .in_0(alu_1_output), .in_1(RF_rdata1), .out(multiplexer_2_out));

  // Notes on the sheet:
  //   contents of IM (hex, n*v repeats v):
  //   0,5,5,2,9,f,6,a
  //   contents of rom_1 (hex, n*v repeats v):
  //   2,1,1
  //   contents of CU (hex, n*v repeats v):
  //   18,38,90,b0,190,130,92,b2,93,b3,94,b4,95,75,51,b1
endmodule
