// Digital circuit 4bit_subtractor.dig as structural Verilog
module _4bit_subtractor (
  input  [3:0] A,
  input  [3:0] B,
  input  S,
  output [3:0] Result,
  output Cout
);

  wire _4bit_full_adder_1_cout;
  wire [3:0] multiplexer_1_out, not_1_out;

  assign not_1_out = ~B;  // Not not_1, 4 bits wide
  Multiplexer #(.Bits(4)) multiplexer_1 (.sel(S), .in_0(B), .in_1(not_1_out), .out(multiplexer_1_out));
  _4bit_full_adder _4bit_full_adder_1 (
    .A(A), .B(multiplexer_1_out), .Cin(S), .S(Result), .Cout(_4bit_full_adder_1_cout));
  not not_2 (Cout, _4bit_full_adder_1_cout);
endmodule
