// Digital circuit ALU.dig as structural Verilog
module ALU (
  input  [3:0] A,
  input  [3:0] B,
  input  [2:0] Control,
  output [3:0] Output,
  output Z_Flag
);

  wire [0:0] _4bit_subtractor_1_cout;
  wire [3:0] _4bit_subtractor_1_result, and_1_out, or_1_out, xor_1_out;

  _4bit_subtractor _4bit_subtractor_1 (
    .A(A), .B(B), .S(Control[0]), .Result(_4bit_subtractor_1_result), .Cout(_4bit_subtractor_1_cout[0]));
  assign and_1_out = A & B;  // And and_1, 4 bits wide
  assign or_1_out = A | B;  // Or or_1, 4 bits wide
  assign xor_1_out = A ^ B;  // XOr xor_1, 4 bits wide
  Multiplexer #(.Selector_Bits(3), .Bits(4)) multiplexer_1 (
    .sel(Control), .in_0(_4bit_subtractor_1_result), .in_1(_4bit_subtractor_1_result), .in_2(and_1_out),
    .in_3(or_1_out), .in_4(xor_1_out), .in_5({3'b000, _4bit_subtractor_1_cout[0]}), .in_6(4'b0000),
    .in_7(4'b0000), .out(Output));
  nor nor_1 (Z_Flag, Output[3], Output[2], Output[1], Output[0]);
endmodule

/* Test case Test ADD:
A B Control Output Z-Flag
loop(A,16)
  loop(B,16)
    (A) (B) 0x0 (A+B) (((A+B)=0)|(((A+B)%16)=0))
  end loop
end loop
*/

/* Test case Test AND:
A B Control Output Z-Flag
loop(A,16)
  loop(B,16)
    (A) (B) 0x2 (A&B) ((A&B)=0)
  end loop
end loop
*/

/* Test case Test XOR:
A B Control Output Z-Flag
loop(A,16)
  loop(B,16)
    (A) (B) 0x4 (A^B) ((A^B)=0)
  end loop
end loop
*/

/* Test case Test SUB:
A B Control Output Z-Flag
loop(A,16)
  loop(B,16)
    (A) (B) 0x1 (A-B) ((A-B)=0)
  end loop
end loop
*/

/* Test case Test OR:
A B Control Output Z-Flag
loop(A,16)
  loop(B,16)
    (A) (B) 0x3 (A|B) ((A|B)=0)
  end loop
end loop
*/

/* Test case Test SLT:
A B Control Output Z-Flag
loop(A,16)
  loop(B,16)
    (A) (B) 0x5 (A<B) ((A<B)=0)
  end loop
end loop
*/
