// Digital circuit PC.dig as structural Verilog
module PC (
  input  clk,
  input  inc,
  output [3:0] PC
);

  wire [3:0] PC_plus_1_s;

  Register #(.Bits(4)) register_1 (.D(PC_plus_1_s), .C(clk), .en(inc), .Q(PC));
  _4bit_full_adder PC_plus_1 (.A(PC), .B(4'b0000), .Cin(1'b1), .S(PC_plus_1_s));  // open: Cout
endmodule
